// Logisim project 14 BIT ALU.circ as structural Verilog: 1 circuit, main circuit main
module main (
  input  Cin,
  input  [31:0] A,
  input  [31:0] B,
  input  [2:0] ALU_OP,
  input  Binv,
  output [31:0] S,
  output Cout,
  output Zero
);

  wire comparator_1_lt;
  wire [4:0] bit_extender_1_out;
  wire [31:0] adder_1_out, AND_out, bit_extender_2_out, multiplexer_1_out, not_1_out, shifter_1_out;

  assign not_1_out = ~B;  // NOT_Gate not_1, 32 bits wide
  Multiplexer #(.width(32), .enable("false")) multiplexer_1 (
    .in0(B), .in1(not_1_out), .out(multiplexer_1_out), .sel(Binv));
  Bit_Extender #(.in_width(32), .out_width(5)) bit_extender_1 (.in(A), .out(bit_extender_1_out));
  assign AND_out = A & B;  // AND_Gate AND, 32 bits wide
  Adder #(.width(32)) adder_1 (.a(A), .b(multiplexer_1_out), .out(adder_1_out), .cin(Cin), .cout(Cout));
  Comparator #(.width(32)) comparator_1 (.a(B), .b(A), .eq(Zero), .lt(comparator_1_lt));  // open: gt
  Shifter #(.width(32)) shifter_1 (.in(B), .\dist (bit_extender_1_out), .out(shifter_1_out));
  assign bit_extender_2_out = {{31{1'b0}}, comparator_1_lt};  // Bit_Extender bit_extender_2
  Multiplexer #(.select(3), .width(32), .enable("false")) multiplexer_2 (
    .in1(AND_out), .in2(bit_extender_2_out), .in3(adder_1_out), .in4(shifter_1_out), .out(S), .sel(ALU_OP));  // open: in0, in5, in6, in7
endmodule
