// Logisim project 14 bit ISA.circ as structural Verilog: 1 circuit, main circuit main
module main (
  input  Clear,
  input  CLR_RAM,
  output [15:0] out_3,
  output out_4
);

  wire clock_1_out, main_1_alu_src, main_1_beq, main_1_binv, main_1_cin, main_1_jump, main_1_mem_to_reg,
       main_1_memread, main_1_memwrite, main_1_reg_dst, main_1_reg_write, main_3_zero;
  wire [2:0] main_1_aluop, multiplexer_2_out;
  wire [13:0] bit_extender_4_out, ram_1_data, rom_1_data;
  wire [15:0] adder_1_out, adder_2_out, bit_extender_1_out, bit_extender_2_out, PC_q, undriven;
  wire [23:0] bit_extender_3_out;
  wire [31:0] bit_extender_5_out, main_2_read_data_1, main_2_read_data_2, main_3_s, multiplexer_3_out,
       multiplexer_5_out, undriven_2;

  Clock clock_1 (.out(clock_1_out));
  Register #(.width(16)) PC (.D(out_3), .Q(PC_q), .clk(clock_1_out), .clr(Clear));  // open: en
  Adder #(.width(16)) adder_1 (.a(16'h1), .b(PC_q), .out(adder_1_out));  // open: cin, cout
  ROM #(.addrWidth(16), .dataWidth(14)) rom_1 (.addr(PC_q), .data(rom_1_data));  // open: sel
  assign bit_extender_1_out = {{9{1'b0}}, rom_1_data[6:0]};  // Bit_Extender bit_extender_1
  Multiplexer #(.width(16), .enable("false")) multiplexer_1 (
    .in0(bit_extender_1_out), .in1(adder_1_out), .sel(main_1_jump));  // open: out
  Multiplexer #(.width(3), .enable("false")) multiplexer_2 (
    .in0(rom_1_data[2:0]), .in1(rom_1_data[5:3]), .out(multiplexer_2_out), .sel(main_1_reg_dst));
  control_unit_main main_1 (
    .ALU_src(main_1_alu_src), .Reg_Write(main_1_reg_write), .OPcode(rom_1_data[13:9]), .ALUop(main_1_aluop),
    .Binv(main_1_binv), .Cin(main_1_cin), .Mem_to_reg(main_1_mem_to_reg), .Reg_dst(main_1_reg_dst),
    .jump(main_1_jump), .MemRead(main_1_memread), .MemWrite(main_1_memwrite), .Beq(main_1_beq));
  Register_File_main main_2 (
    .Write_Enable(main_1_reg_write), .Write_Data(multiplexer_5_out), .Read_Data_1(main_2_read_data_1),
    .Read_Reg_1(rom_1_data[8:6]), .Read_Data_2(main_2_read_data_2), .Read_Reg_2(rom_1_data[5:3]),
    .Write_Reg(multiplexer_2_out), .CLK(clock_1_out));
  Multiplexer #(.width(32), .enable("false")) multiplexer_3 (
    .in0(main_2_read_data_2), .in1(undriven_2), .out(multiplexer_3_out), .sel(main_1_alu_src));
  Bit_Extender #(.in_width(32)) bit_extender_2 (.in(undriven_2), .out(bit_extender_2_out));
  Adder #(.width(16)) adder_2 (.a(undriven), .b(bit_extender_2_out), .out(adder_2_out));  // open: cin, cout
  and and_1 (out_4, main_1_beq, main_3_zero);
  _14_BIT_ALU_main main_3 (
    .Cin(main_1_cin), .A(main_2_read_data_1), .B(multiplexer_3_out), .ALU_OP(main_1_aluop), .S(main_3_s),
    .Binv(main_1_binv), .Zero(main_3_zero));  // open: Cout
  Multiplexer #(.width(16), .enable("false")) multiplexer_4 (
    .in0(undriven), .in1(adder_2_out), .out(out_3), .sel(out_4));
  Bit_Extender #(.in_width(32), .out_width(24)) bit_extender_3 (.in(main_3_s), .out(bit_extender_3_out));
  Bit_Extender #(.in_width(32), .out_width(14)) bit_extender_4 (.in(main_2_read_data_2), .out(bit_extender_4_out));
  RAM #(.addrWidth(24), .dataWidth(14), .bus("separate")) ram_1 (
    .addr(bit_extender_3_out), .din(bit_extender_4_out), .data(ram_1_data), .str(main_1_memwrite),
    .clk(clock_1_out), .ld(main_1_memread), .clr(CLR_RAM));  // open: sel
  Multiplexer #(.width(32), .enable("false")) multiplexer_5 (
    .in1(bit_extender_5_out), .out(multiplexer_5_out), .sel(main_1_mem_to_reg));  // open: in0
  assign bit_extender_5_out = {{18{1'b0}}, ram_1_data};  // Bit_Extender bit_extender_5

  // Notes on the sheet:
  //   contents of rom_1 (hex, n*v repeats v):
  //   12 32
endmodule
