// Logisim project control unit.circ as structural Verilog: 1 circuit, main circuit main
module main (
  input  [4:0] OPcode,
  output MemWrite,
  output MemRead,
  output Mem_to_reg,
  output Binv,
  output Cin,
  output Beq,
  output Reg_Write,
  output ALU_src,
  output jump,
  output Reg_dst,
  output [2:0] ALUop
);

  wire decoder_1_out0, decoder_1_out3, decoder_1_out4, decoder_1_out6, decoder_1_out7, decoder_1_out8,
       decoder_1_out9;
  wire [3:0] bit_extender_1_out;

  Bit_Extender #(.in_width(5), .out_width(4)) bit_extender_1 (.in(OPcode), .out(bit_extender_1_out));
  Decoder #(.select(4), .enable("false")) decoder_1 (
    .out0(decoder_1_out0), .out1(MemWrite), .out2(Binv), .out3(decoder_1_out3), .out4(decoder_1_out4),
    .out5(Beq), .out6(decoder_1_out6), .out7(decoder_1_out7), .out8(decoder_1_out8), .out9(decoder_1_out9),
    .out10(jump), .sel(bit_extender_1_out));  // open: out11, out12, out13, out14, out15
  or or_1 (ALUop[2], Beq, decoder_1_out6, decoder_1_out9);
  or or_2 (ALUop[1], MemWrite, Binv, decoder_1_out4, Beq, decoder_1_out7, decoder_1_out8, decoder_1_out9, jump);
  or or_3 (ALUop[0], decoder_1_out3, decoder_1_out4, Beq, decoder_1_out9);
  or or_4 (Reg_Write, Binv, decoder_1_out3, decoder_1_out4, decoder_1_out6, decoder_1_out7, decoder_1_out8, jump);
  or or_5 (Reg_dst, MemWrite, decoder_1_out4, Beq, decoder_1_out8, jump);
  or or_6 (ALU_src, MemWrite, decoder_1_out4, decoder_1_out8, jump);

  assign Cin = Binv;
  assign Mem_to_reg = jump;
  assign MemRead = jump;
endmodule
